// Logisim project PROJETO.circ as structural Verilog
module ADD_1 (
  input  a,
  input  b,
  input  Vem_1,
  output S,
  output vai_1
);

  wire and_1_out, and_2_out, or_1_out, xor_1_out;

  xor xor_1 (xor_1_out, b, a);
  or or_1 (or_1_out, Vem_1, b);
  and and_1 (and_1_out, b, Vem_1);
  and and_2 (and_2_out, or_1_out, a);
  xor xor_2 (S, Vem_1, xor_1_out);
  or or_2 (vai_1, and_2_out, and_1_out);
endmodule

module add_4 (
  input  [3:0] in_1,
  input  [3:0] in_2,
  output out_3,
  output [3:0] out_4
);

  wire add_1_2_vai_1, add_1_3_vai_1, add_1_4_vai_1;

  ADD_1 add_1_1 (.S(out_4[3]), .vai_1(out_3), .a(in_2[3]), .b(in_1[3]), .Vem_1(add_1_2_vai_1));
  ADD_1 add_1_2 (.S(out_4[2]), .vai_1(add_1_2_vai_1), .a(in_2[2]), .b(in_1[2]), .Vem_1(add_1_3_vai_1));
  ADD_1 add_1_3 (.S(out_4[1]), .vai_1(add_1_3_vai_1), .a(in_2[1]), .b(in_1[1]), .Vem_1(add_1_4_vai_1));
  ADD_1 add_1_4 (.S(out_4[0]), .vai_1(add_1_4_vai_1), .a(in_2[0]), .b(in_1[0]), .Vem_1(1'b0));
endmodule

module comp2 (
  input  [3:0] in_1,
  output [3:0] out_2
);

  wire [3:0] not_4_out;

  not not_1 (not_4_out[3], in_1[3]);
  not not_2 (not_4_out[1], in_1[1]);
  not not_3 (not_4_out[2], in_1[2]);
  not not_4 (not_4_out[0], in_1[0]);
  add_4 add_4_1 (.in_2(not_4_out), .in_1(4'b0001), .out_4(out_2));  // open: out_3
endmodule

module sub (
  input  [3:0] B,
  input  [3:0] A,
  output [3:0] out_3
);

  wire [3:0] comp2_1_out_2;

  comp2 comp2_1 (.in_1(B), .out_2(comp2_1_out_2));
  add_4 add_4_1 (.in_2(A), .in_1(comp2_1_out_2), .out_4(out_3));  // open: out_3
endmodule
